// Logisim project Fibonacci Genrator_20BIT103,039,077,021,139.circ as structural Verilog: 1 circuit, main circuit main
module main (
);

  wire and_1_out, and_2_out, and_3_out, button_1_out, clock_1_out, controlled_buffer_1_out,
       controlled_buffer_2_out, controlled_buffer_3_out, controlled_buffer_4_out, controlled_buffer_5_out,
       controlled_buffer_7_out, counter_2_q, demultiplexer_1_out0, demultiplexer_1_out1,
       demultiplexer_1_out2, demultiplexer_2_out0, demultiplexer_2_out1, not_1_out, not_2_out, not_3_out,
       not_4_out, s_r_ff_1_q, s_r_ff_2_q, s_r_ff_3_q, s_r_ff_3_qn;
  wire [1:0] counter_1_q;
  wire [31:0] adder_1_out, controlled_buffer_8_out, register_1_q, register_2_q, register_3_q;

  Clock clock_1 (.out(clock_1_out));
  Button button_1 (.out(button_1_out));
  S_R_Flip_Flop s_r_ff_1 (.Q(s_r_ff_1_q), .preset(button_1_out), .reset(and_2_out));  // open: S, clk, R, Qn, en
  and and_1 (and_1_out, clock_1_out, s_r_ff_1_q);
  not not_1 (not_1_out, and_1_out);
  and and_2 (and_2_out, not_4_out, not_2_out);
  S_R_Flip_Flop s_r_ff_2 (.Q(s_r_ff_2_q), .preset(and_2_out), .reset(button_1_out));  // open: S, clk, R, Qn, en
  Demultiplexer #(.select(2), .enable("false")) demultiplexer_1 (
    .out0(demultiplexer_1_out0), .out1(demultiplexer_1_out1), .out2(demultiplexer_1_out2), .in(and_1_out),
    .sel(counter_1_q));  // open: out3
  Counter #(.width(2), .max('h3)) counter_1 (
    .Q(counter_1_q), .clk(not_1_out), .clr(button_1_out));  // open: load, D, count, carry
  not not_2 (not_2_out, not_4_out);
  and and_3 (and_3_out, clock_1_out, s_r_ff_2_q);
  not not_3 (not_3_out, and_3_out);
  assign controlled_buffer_1_out = demultiplexer_1_out0 ? demultiplexer_1_out0 : 1'bz;  // Controlled_Buffer controlled_buffer_1
  assign controlled_buffer_2_out = demultiplexer_1_out0 ? demultiplexer_1_out0 : 1'bz;  // Controlled_Buffer controlled_buffer_2
  assign controlled_buffer_3_out = demultiplexer_1_out1 ? demultiplexer_1_out1 : 1'bz;  // Controlled_Buffer controlled_buffer_3
  assign controlled_buffer_4_out = demultiplexer_1_out2 ? demultiplexer_1_out2 : 1'bz;  // Controlled_Buffer controlled_buffer_4
  not not_4 (not_4_out, demultiplexer_1_out2);
  Demultiplexer #(.enable("false")) demultiplexer_2 (
    .out0(demultiplexer_2_out0), .out1(demultiplexer_2_out1), .in(and_3_out), .sel(counter_2_q));
  Counter #(.width(1), .max('h1)) counter_2 (
    .Q(counter_2_q), .clk(not_3_out), .clr(button_1_out));  // open: load, D, count, carry
  assign controlled_buffer_5_out = demultiplexer_2_out0 ? demultiplexer_2_out0 : 1'bz;  // Controlled_Buffer controlled_buffer_5
  assign controlled_buffer_3_out = demultiplexer_2_out1 ? demultiplexer_2_out1 : 1'bz;  // Controlled_Buffer controlled_buffer_6
  assign controlled_buffer_7_out = demultiplexer_2_out1 ? demultiplexer_2_out1 : 1'bz;  // Controlled_Buffer controlled_buffer_7
  Pull_Resistor pull_resistor_1 (.node(controlled_buffer_2_out));
  Pull_Resistor pull_resistor_2 (.node(controlled_buffer_4_out));
  Pull_Resistor pull_resistor_3 (.node(controlled_buffer_5_out));
  Pull_Resistor pull_resistor_4 (.node(controlled_buffer_1_out));
  Pull_Resistor pull_resistor_5 (.node(controlled_buffer_7_out));
  Pull_Resistor pull_resistor_6 (.node(controlled_buffer_3_out));
  // Probe on register_1_q
  assign controlled_buffer_8_out = s_r_ff_3_qn ? 32'h1 : 32'bz;  // Controlled_Buffer controlled_buffer_8
  S_R_Flip_Flop s_r_ff_3 (
    .Q(s_r_ff_3_q), .Qn(s_r_ff_3_qn), .preset(controlled_buffer_4_out), .reset(controlled_buffer_2_out));  // open: S, clk, R, en
  assign controlled_buffer_8_out = s_r_ff_3_q ? register_3_q : 32'bz;  // Controlled_Buffer controlled_buffer_9
  Register #(.width(32)) register_1 (
    .D(register_2_q), .Q(register_1_q), .clk(controlled_buffer_7_out), .clr(controlled_buffer_1_out));  // open: en
  Register #(.width(32)) register_2 (
    .D(controlled_buffer_8_out), .Q(register_2_q), .clk(controlled_buffer_3_out),
    .clr(controlled_buffer_1_out));  // open: en
  Register #(.width(32)) register_3 (
    .D(adder_1_out), .Q(register_3_q), .clk(controlled_buffer_5_out), .clr(controlled_buffer_1_out));  // open: en
  Adder #(.width(32)) adder_1 (.a(register_1_q), .b(register_2_q), .out(adder_1_out));  // open: cin, cout

  // Notes on the sheet:
  //   Rishil Trivedi(GR)
  //   VIshwas Darji
  //   Ravi Prajapati
  //   Jay Suthar
  //   Amit Sagathiya
  //   Clock (Frequency-2 Hz)
  //   Switch for Reset
  //   Name               Roll. No
  //   20BIT103
  //   20BIT039
  //   20BIT021
  //   20BIT077
  //   20BIT139
  //   Counter working as Loop
  //   Fibonacci Genrator
  //   A=0
  //   Assigning values B=C=1
  //   Numbers in Decimal
  //   Registers as variable 
  //   A
  //   B
  //   C
  //   A+B
endmodule
